# Fritzing sketch TP1_Semaforos_v_3_2 (saved by Fritzing 0.9.3b)
breadboards: 1

parts:
  Componente1 = Arduino Uno (Rev3)
  R1 = Resistor [tolerance=±5% resistance=220 package=THT]
  R2 = Resistor [tolerance=±5% resistance=220 package=THT]
  R3 = Resistor [tolerance=±5% resistance=220 package=THT]
  R4 = Resistor [tolerance=±5% resistance=220 package=THT]
  R5 = Resistor [tolerance=±5% resistance=220 package=THT]
  R6 = Resistor [tolerance=±5% resistance=220 package=THT]
  LED3 = LED - 3mm [color="Green (560nm)" package="3 mm [THT]"]
  LED2 = LED - 3mm [color="Yellow (585nm)" package="3 mm [THT]"]
  LED1 = LED - 3mm [color="Red (635nm)" package="3 mm [THT]"]
  LED6 = LED - 3mm [color="Red (633nm)" package="3 mm [THT]"]
  LED5 = LED - 3mm [color="Yellow (585nm)" package="3 mm [THT]"]
  LED4 = LED - 3mm [color="Green (570nm)" package="3 mm [THT]"]
  C1 = Electrolytic Capacitor [capacitance=100µF package="100 mil [THT, electrolytic]"]

nets:
  N1: Componente1.D8, LED6.anode
  N2: Componente1.GND, R1.Pin_1, R2.Pin_1, R3.Pin_1, R4.Pin_1, R5.Pin_1, R6.Pin_1, C1.-
  N3: Componente1.D3_PWM, LED1.anode
  N4: Componente1.D4, LED2.anode
  N5: Componente1.D5_PWM, LED3.anode
  N6: Componente1.D6_PWM, LED4.anode
  N7: Componente1.D7, LED5.anode
  N8: Componente1.5V, C1.+
  N9: R1.Pin_0, LED1.cathode
  N10: R2.Pin_0, LED2.cathode
  N11: R3.Pin_0, LED3.cathode
  N12: R4.Pin_0, LED4.cathode
  N13: R5.Pin_0, LED5.cathode
  N14: R6.Pin_0, LED6.cathode
